# Fritzing sketch Untitled Sketch 2 (saved by Fritzing 0.9.3b)

parts:
  LCD1 = LCD screen  # not connected
  Raspberry_Pi_1 = Raspberry Pi 3 [part_number=RPI-3-V1.2]
  DIN1 = DIN-5 jack (MIDI) [package=THT]
  S1 = Pushbutton [package="[THT]"]
  LED1 = LED - 5mm [color="Red (633nm)" package="5 mm [THT]"]  # not connected
  C1 = Ceramic Capacitor [capacitance=100nF package="100 mil [THT, multilayer]"]
  C2 = Electrolytic Capacitor [capacitance=1µF package="100 mil [THT, electrolytic]"]  # not connected
  CONN1 = USB connector [package=THT]  # not connected
  R1 = Resistor [tolerance=±5% resistance=220 package=THT]
  R2 = Resistor [tolerance=±5% resistance=220 package=THT]
  L1 = Inductor [package="400 mil [THT]"]
  L2 = Inductor [package="400 mil [THT]"]
  J1 = Piezo Speaker

nets:
  N1: Raspberry_Pi_1.3v3, R2.Pin_1
  N2: Raspberry_Pi_1.GPIO2, S1.Pin_3, S1.Pin_4, C1.0
  N3: Raspberry_Pi_1.GND, S1.Pin_1, S1.Pin_2, C1.1, J1.pin1
  N4: Raspberry_Pi_1.GPIO13, J1.pin2
  N5: Raspberry_Pi_1.GPIO14, R1.Pin_1
  N6: DIN1.5, L2.pin_0
  N7: DIN1.4, L1.pin_0

notes:
  MIDI OUT
  BUZZER
  10 Ом
  33 Ом
  100 нФ
  FB 1K@100MHz
  BUTTON
