# Fritzing sketch Untitled Sketch 3 (saved by Fritzing 0.9.3b)
stripboards: 1

parts:
  Raspberry_Pi_2 = Raspberry Pi 3 [part_number=RPI-3-V1.2]
  LCD2 = LCD screen [part_number=5]
  R1 = Trimmer Potentiometer [maximum_resistance=10kΩ package=THT]
  R2 = Resistor [tolerance=±5% resistance=220 package=THT]
  C5 = Electrolytic Capacitor [capacitance=1µF package="100 mil [THT, electrolytic]"]

nets:
  N1: Raspberry_Pi_2.GPIO11, LCD2.DB7
  N2: Raspberry_Pi_2.GPIO6, LCD2.DB6
  N3: Raspberry_Pi_2.GPIO19, LCD2.DB5
  GND: Raspberry_Pi_2.GND, Raspberry_Pi_2.GPIO12, LCD2.VSS, LCD2.RS, LCD2.E, R1.leg1, C5.+
  N4: Raspberry_Pi_2.GPIO20, LCD2.DB4
  5V: Raspberry_Pi_2.5V, LCD2.VDD, R1.leg2, R2.Pin_0, C5.-
  N5: LCD2.V0, R1.wiper

notes:
  100 uF
